# Fritzing sketch 16-seg-display-v2 (saved by Fritzing 0.9.2b)
circuit board: 3.05cm x 5.7cm
breadboards: 1

parts:
  IC1 = PICAXE-18 [package=THT]
  IC2 = PICAXE-18 [package=THT]
  J7 = male pin header, 7 pins [form="♂ (male)"]
  J6 = male pin header, 7 pins [form="♂ (male)"]
  J12 = male pin header, 4 pins [form="♂ (male)"]
  J10 = male pin header, 1 pin [form="♂ (male)"]
  J4 = male pin header, 4 pins [form="♂ (male)"]
  J9 = male pin header, 1 pin [form="♂ (male)"]
  J13 = male pin header, 1 pin [form="♂ (male)"]
  J8 = male pin header, 1 pin [form="♂ (male)"]
  R4 = Resistor [tolerance=±5% resistance=220 package=THT]
  R5 = Resistor [tolerance=±5% resistance=220 package=THT]
  R6 = Resistor [tolerance=±5% resistance=220 package=THT]
  R7 = Resistor [tolerance=±5% resistance=220 package=THT]
  R8 = Resistor [tolerance=±5% resistance=220 package=THT]
  R9 = Resistor [tolerance=±5% resistance=220 package=THT]
  R10 = Resistor [tolerance=±5% resistance=220 package=THT]
  R11 = Resistor [tolerance=±5% resistance=220 package=THT]
  R12 = Resistor [tolerance=±5% resistance=220 package=THT]
  R13 = Resistor [tolerance=±5% resistance=220 package=THT]
  R14 = Resistor [tolerance=±5% resistance=220 package=THT]
  R15 = Resistor [tolerance=±5% resistance=220 package=THT]
  R16 = Resistor [tolerance=±5% resistance=220 package=THT]
  R17 = Resistor [tolerance=±5% resistance=220 package=THT]
  R18 = Resistor [tolerance=±5% resistance=220 package=THT]
  R19 = Resistor [tolerance=±5% resistance=220 package=THT]
  J15 = male pin header, 2 pins [form="♂ (male)"]
  J16 = male pin header, 2 pins [form="♂ (male)"]
  J14 = male pin header, 2 pins [form="♂ (male)"]

nets:
  N1: IC1.In_2, IC1.Out_3, IC2.In_2, IC2.Out_3, J15.pin2, J16.pin2, J14.pin2
  N2: IC1.Serial_Out, R6.Pin_0
  N3: IC1.Serial_In, R4.Pin_0
  N4: IC1.Reset, R5.Pin_0
  N5: IC1.0V, R7.Pin_0
  N6: IC1.Out_0, R8.Pin_0
  N7: IC1.Out_1, R9.Pin_0
  N8: IC1.Out_2, R10.Pin_0
  N9: IC1.Out_4, IC2.In_6
  N10: IC1.Out_5, IC2.Out_5, J12.pin1, J4.pin1
  N11: IC1.Out_6, IC2.Out_6, J12.pin2, J4.pin2
  N12: IC1.Out_7, IC2.Out_7, J12.pin3, J4.pin3
  N13: IC1.+V, IC2.+V, J12.pin4, J4.pin4
  N14: IC1.In_6, J13.pin1
  N15: IC1.In_7, R18.Pin_0
  N16: IC1.In_0, IC1.In_1, IC2.In_0, IC2.In_1, J15.pin1, J16.pin1, J14.pin1
  N17: IC2.Serial_Out, R12.Pin_0
  N18: IC2.Serial_In, R15.Pin_0
  N19: IC2.Reset, R14.Pin_0
  N20: IC2.0V, R16.Pin_0
  N21: IC2.Out_0, R17.Pin_0
  N22: IC2.Out_1, R11.Pin_0
  N23: IC2.Out_2, R13.Pin_0
  N24: IC2.Out_4, J10.pin1
  N25: IC2.In_7, R19.Pin_0
  N26: J7.pin1, R13.Pin_1
  N27: J7.pin2, R11.Pin_1
  N28: J7.pin3, R17.Pin_1
  N29: J7.pin4, R16.Pin_1
  N30: J7.pin5, R14.Pin_1
  N31: J7.pin6, R15.Pin_1
  N32: J7.pin7, R12.Pin_1
  N33: J6.pin1, R10.Pin_1
  N34: J6.pin2, R9.Pin_1
  N35: J6.pin3, R8.Pin_1
  N36: J6.pin4, R7.Pin_1
  N37: J6.pin5, R5.Pin_1
  N38: J6.pin6, R4.Pin_1
  N39: J6.pin7, R6.Pin_1
  N40: J9.pin1, R19.Pin_1
  N41: J8.pin1, R18.Pin_1

notes:
  +
  Out
  -
  Data
  OE
  Lat
  Clk
  Clr
